# Fritzing sketch Fritzing_lab5 (saved by Fritzing 0.9.9b)
breadboards: 1

parts:
  Part1 = Arduino Uno (Rev3)
  LED1 = LED - 5mm [color="Green (560nm)" current=0.030 package="5 mm [THT]"]
  LED2 = LED - 5mm [color="Red (633nm)" current=0.030 package="5 mm [THT]"]
  LED3 = LED - 5mm [color="Blue (505nm)" current=0.030 package="5 mm [THT]"]
  LED4 = LED - 5mm [color="Yellow (592nm)" current=0.030 package="5 mm [THT]"]
  LED5 = smd LED [color="Green (565nm)" current=0.030 package="0603 [SMD]"]
  R1 = Resistor [tolerance=±5% power=0.25 resistance=220 package=THT]
  R2 = Resistor [tolerance=±5% power=0.25 resistance=220 package=THT]
  R3 = Resistor [tolerance=±5% power=0.25 resistance=220 package=THT]
  R4 = Resistor [tolerance=±5% power=0.25 resistance=220 package=THT]
  R5 = Resistor [tolerance=±5% power=0.25 resistance=220 package=THT]
  R6 = Rotary Potentiometer (Large) [maximum_resistance=100kΩ package=THT]

nets:
  N1: Part1.A0, R6.wiper
  N2: Part1.GND, LED2.cathode, LED3.cathode, LED4.cathode, LED5.cathode, R6.leg2
  N3: Part1.D2, R1.Pin_1
  N4: Part1.D3_PWM, R2.Pin_1
  N5: Part1.D4, R3.Pin_1
  N6: Part1.D5_PWM, R4.Pin_1
  N7: Part1.D6_PWM, R5.Pin_1
  N8: Part1.3V3, R6.leg1
  N9: LED1.anode, R5.Pin_0
  N10: LED2.anode, R4.Pin_0
  N11: LED3.anode, R3.Pin_0
  N12: LED4.anode, R2.Pin_0
  N13: LED5.anode, R1.Pin_0
